# Fritzing sketch Patch01-Kick_Sci-Fi_Gun_with_VCF (saved by Fritzing 0.9.2b)

parts:
  Part1 = Ns1 Nanosynth by SoundMachines

nets:
  N1: Part1.GATE#103, Part1.GATE#130
  N2: Part1.→#120, Part1.OUT
  N3: Part1.←#121, Part1.CV
  N4: Part1.GATE#131, Part1.BT_1
  N5: Part1.←LP, Part1.→#148
  N6: Part1.←#152, Part1.AMP

notes:
  VCA
  VOLUME OUT: 5
  INITIAL: 5
  VCF
  FREQ: 10
  RESONANCE: 10
  ADSR
  ATTACK: 0
  DECAY: 7.5
  SUSTAIN: 0
  RELEASE: 7.5
  ATTENS
  ATTEN1: 2.5
  By pressing BUTTON1 or on any part of the Ribbon you will trigger a sound similar to a Kick sound, by increasing ATTEN1 the sound will begin to be similar to a Sci-Fi Gun.
  Change timbre by turning sligtly down RESONANCE or add distortion by raising the INITIAL knob (Be careful when cranking up the INITIAL knob, always turn down the VOLUME OUT knob before).

custom parts:
  Ns1 Nanosynth by SoundMachines: The NS1nanosynth synthesizer is tiny 220x85mm analog modular synthesizer coupled with an Arduino Micro platform. NS1nanosynth is a good compromise between complexity and usability. It's a Maker synth, totally hackable and customazable yet a good entry level device, and on a budget.
