# Fritzing sketch NS1patch1vco-vcf-vca (saved by Fritzing 0.9.2b)

parts:
  Componente1 = Ns1 Nanosynth by SoundMachines

nets:
  N1: Componente1.SAW, Componente1.→#145
  N2: Componente1.←LP, Componente1.→#149
  N3: Componente1.←, Componente1.AMP

notes:
  Try changing the sound source including the two types of noise and, why not, the two LFOs at maximum frequency!
  VCA INITIAL: 5
  The simplest patch of any subtractive synth: VCO into VCF into VCA. From here you start getting familiarity with basic sounds of the NS1
  VCF FREQ: 10
  VCF RESO: 0

custom parts:
  Ns1 Nanosynth by SoundMachines: The NS1nanosynth synthesizer is tiny 220x85mm analog modular synthesizer coupled with an Arduino Micro platform. NS1nanosynth is a good compromise between complexity and usability. It's a Maker synth, totally hackable and customazable yet a good entry level device, and on a budget.
