# Fritzing sketch NS1patch2pwm (saved by Fritzing 0.9.2b)

parts:
  Componente1 = Ns1 Nanosynth by SoundMachines

nets:
  N1: Componente1.TRI, Componente1.PWM
  N2: Componente1.SQU, Componente1.→#145
  N3: Componente1.←LP, Componente1.→#149
  N4: Componente1.←, Componente1.AMP

notes:
  VCA INITIAL: 5
  Creating the classic Pulse Width Modulated sound is easy! Just add an LFO at very low frequency that enter into the PWM input of the VCO!
  VCF FREQ: 10
  VCF RESO: 0
  VCO FREQ: 3
  VCO PW: 2
  LFO FREQ1: 0
  Changing the PW setting will 'offset' the amount of the effect. You can also attenuate the LFO output and/or try the square output

custom parts:
  Ns1 Nanosynth by SoundMachines: The NS1nanosynth synthesizer is tiny 220x85mm analog modular synthesizer coupled with an Arduino Micro platform. NS1nanosynth is a good compromise between complexity and usability. It's a Maker synth, totally hackable and customazable yet a good entry level device, and on a budget.
