# Fritzing sketch NS1patch3vco-vcf-lfo (saved by Fritzing 0.9.2b)

parts:
  Componente1 = Ns1 Nanosynth by SoundMachines

nets:
  N1: Componente1.TRI#71, Componente1.→#119
  N2: Componente1.TRI#78, Componente1.→#126
  N3: Componente1.CV#107, Componente1.←#121
  N4: Componente1.SAW, Componente1.→#145
  N5: Componente1.←#127, Componente1.CV#142
  N6: Componente1.←LP, Componente1.→#149
  N7: Componente1.←#152, Componente1.AMP

notes:
  VCA INITIAL: 5
  Learn how to modulate oscillators and filters with LFOs and attenuators. This is a basic setting that will give a lot of sonic possibilities!
  VCF FREQ: 2
  VCF RESO: 0 to 8
  VCO FREQ: 2
  LFO FREQ1: play!
  LFO FREQ2: play!
  Try also square output!
  ATTEN1 regulates the amount of FM to the VCO and ATTEN2 the modulation amount to the filter FREQ. You can play with those parameters to change the output!

custom parts:
  Ns1 Nanosynth by SoundMachines: The NS1nanosynth synthesizer is tiny 220x85mm analog modular synthesizer coupled with an Arduino Micro platform. NS1nanosynth is a good compromise between complexity and usability. It's a Maker synth, totally hackable and customazable yet a good entry level device, and on a budget.
