# Fritzing sketch NS1patch5midi (saved by Fritzing 0.9.2b)

parts:
  Componente1 = Ns1 Nanosynth by SoundMachines

nets:
  N1: Componente1.DAC0, Componente1.V/OCT
  N2: Componente1.DAC1, Componente1.PWM
  N3: Componente1.5, Componente1.GATE
  N4: Componente1.SAW, Componente1.→#145
  N5: Componente1.→#119, Componente1.OUT#132
  N6: Componente1.←#121, Componente1.CV#142
  N7: Componente1.→#126, Componente1.OUT#133
  N8: Componente1.←#127, Componente1.CV#150
  N9: Componente1.←LP, Componente1.→#149
  N10: Componente1.←#152, Componente1.AMP

notes:
  VCA INITIAL: 0
  Connect your NS1 to your MIDI host! either PC/MAC or any MIDI over USB capable platform!!!! Remember that NS1 waits for messages on MIDI channel #1!
  VCF FREQ: 5 to 0
  VCF RESO: 7
  VCO FREQ: 0
  ADSR: start with all the params at zero except the sustain, then play with them to understand the effect!
  ATTEN1 regulates the amount of ADSR to the VCA. Start at 0 and slowly rise the amount. ATTEN2 regulates the amount to the FREQ of the filter.
  NS1nanosynth is a MIDI class compliant device. In its current implementation listens to NOTE ON / NOTE OFF (pin 5 is the GATE), PITCH+PITCHBEND (DAC0) and MODWHEEL (DAC1) messages on MIDI channel #1. Filters out notes lower than C2! As the MIDI CLOCK is not used in the current implementation you should turn this message off.

custom parts:
  Ns1 Nanosynth by SoundMachines: The NS1nanosynth synthesizer is tiny 220x85mm analog modular synthesizer coupled with an Arduino Micro platform. NS1nanosynth is a good compromise between complexity and usability. It's a Maker synth, totally hackable and customazable yet a good entry level device, and on a budget.
