# Fritzing sketch NS1patch8logic_xor_ringmod (saved by Fritzing 0.9.2b)

parts:
  Componente1 = Ns1 Nanosynth by SoundMachines

nets:
  N1: Componente1.SQU#72, Componente1.NAND_←#177
  N2: Componente1.SQU#73, Componente1.OR_←#174
  N3: Componente1.SQU#80, Componente1.OR_←#173
  N4: Componente1.SQU#81, Componente1.NAND_←#176
  N5: Componente1.→#125, Componente1.OUT
  N6: Componente1.←#127, Componente1.CV
  N7: Componente1.GATE, Componente1.BT_3
  N8: Componente1.→#144, Componente1.AND_→
  N9: Componente1.←LP, Componente1.→#149
  N10: Componente1.←#152, Componente1.AMP
  N11: Componente1.AND_←#170, Componente1.OR_→
  N12: Componente1.AND_←#171, Componente1.NAND_→

notes:
  DIGITAL RING MODULATOR
  We use LFO1 and LFO2 at the audio frequency. You can use one LFO and the VCO (square) also.
  start with LFO1 and LFO2 frequency to the maximum and decrease them slightly one at a time until you get that dissonant bell tone...
  Press button3 to trigger the bell!
  VCA INITIAL: 0
  VCF FREQ: 3
  VCF RES: 7/8
  ADSR: enable SLOW by shorting the two patchpoints with a nanopatch.
  Attack and Decay = 0.
  Sustain: 5 and Release:10
  ATTEN2 = 8 (this sets the maximum VCA volume, raise for distortion!)

custom parts:
  Ns1 Nanosynth by SoundMachines: The NS1nanosynth synthesizer is tiny 220x85mm analog modular synthesizer coupled with an Arduino Micro platform. NS1nanosynth is a good compromise between complexity and usability. It's a Maker synth, totally hackable and customazable yet a good entry level device, and on a budget.
