# Fritzing sketch NS1patch9battling_lfos (saved by Fritzing 0.9.2b)

parts:
  Componente1 = Ns1 Nanosynth by SoundMachines

nets:
  N1: Componente1.C1, Componente1.MIX/3←#82
  N2: Componente1.TRI#71, Componente1.MIX/3←#83
  N3: Componente1.TRI#79, Componente1.MIX/3←#84
  N4: Componente1.MIX/3→, Componente1.CV#142
  N5: Componente1.V/OCT, Componente1.HLD
  N6: Componente1.SUB, Componente1.→#144
  N7: Componente1.→#125, Componente1.OUT
  N8: Componente1.←#127, Componente1.CV#151
  N9: Componente1.←LP, Componente1.→#149
  N10: Componente1.←#152, Componente1.AMP

notes:
  BATTLING LFOs
  We use LFO1 and LFO2 mixed together along with one of the controllers. We use MIX/3 that divides by three each inputs before summing. The output goes straight into VCF CV.
  The rest is a classic patch that uses the VCO subosc to obtain a great square wave sound.
  Play with the ribbon, make your synth talk!!!!!
  VCA INITIAL: 0
  VCF FREQ: 3-4
  VCF RES:7-8
  ADSR: enable SLOW by shorting the two patchpoints with a nanopatch.
  Attack: 2, Decay: 0.
  Sustain: 10 and Release: 3
  ATTEN2 = 8 (this sets the maximum VCA volume, raise for distortion!)
  When you need to use SQU/SUB outputs on the VCO make sure that PW pot is >0!!!!

custom parts:
  Ns1 Nanosynth by SoundMachines: The NS1nanosynth synthesizer is tiny 220x85mm analog modular synthesizer coupled with an Arduino Micro platform. NS1nanosynth is a good compromise between complexity and usability. It's a Maker synth, totally hackable and customazable yet a good entry level device, and on a budget.
